# Fritzing sketch eeprom_writer (saved by Fritzing 0.9.3b)
breadboards: 1

parts:
  Part1 = Arduino Nano (Rev3.0)
  U1 = 74HC595 [package="DIP16 [THT]"]
  U2 = 74HC595 [package="DIP16 [THT]"]
  IC1 = IC, DIP package, 24 pins [chip_label=28C16]
  R1 = Resistor [tolerance=±5% resistance=10k package=THT]
  R2 = Resistor [tolerance=±5% resistance=10k package=THT]
  R3 = Resistor [tolerance=±5% resistance=10k package=THT]
  R4 = Resistor Mini [tolerance=±5% resistance=10k package=THT]
  R5 = Resistor Mini [tolerance=±5% resistance=10k package=THT]
  R6 = Resistor Mini [tolerance=±5% resistance=10k package=THT]

nets:
  GND: Part1.GND, U1.GND, U1.OE, U2.GND, U2.OE, IC1.pin12, R1.Pin_0, R2.Pin_0, R3.Pin_0
  N1: Part1.D2, U1.SH_CP, U2.SH_CP, R3.Pin_1
  N2: Part1.D3, U1.ST_CP, U2.ST_CP, R2.Pin_1
  N3: Part1.D4, U1.DS, R1.Pin_1
  N4: Part1.D5, IC1.pin9
  N5: Part1.D6, IC1.pin10
  N6: Part1.D7, IC1.pin11
  N7: Part1.D8, IC1.pin13
  N8: Part1.D9, IC1.pin14
  N9: Part1.D10, IC1.pin15
  N10: Part1.D11/MOSI, IC1.pin16
  N11: Part1.D12/MISO, IC1.pin17
  VCC: Part1.5V, U1.MR, U1.VCC, U2.MR, U2.VCC, IC1.pin24, R4.Pin_0, R5.Pin_0, R6.Pin_0
  N12: Part1.A2, IC1.pin21, R4.Pin_1
  N13: Part1.A1, IC1.pin20, R5.Pin_1
  N14: Part1.A0, IC1.pin18, R6.Pin_1
  N15: U1.Q1, IC1.pin7
  N16: U1.Q2, IC1.pin6
  N17: U1.Q3, IC1.pin5
  N18: U1.Q4, IC1.pin4
  N19: U1.Q5, IC1.pin3
  N20: U1.Q6, IC1.pin2
  N21: U1.Q7, IC1.pin1
  N22: U1.Q7', U2.DS
  N23: U1.Q0, IC1.pin8
  N24: U2.Q1, IC1.pin22
  N25: U2.Q2, IC1.pin19
  N26: U2.Q0, IC1.pin23

custom parts:
  Resistor Mini: A generic resistor (0.25W)
